// Logisim project CS2010.circ as structural Verilog: 18 circuits, main circuit CS2010
module CS2010 (
);

  wire CLOCK_out, RESET___START_out, uc_1_cpc, uc_1_csp, uc_1_dsp, uc_1_i_omdr, uc_1_inm, uc_1_ipc, uc_1_isp,
       uc_1_rac, uc_1_rmem, uc_1_rpc, uc_1_rsp, uc_1_srw, uc_1_stop, uc_1_wac, uc_1_wir, uc_1_wmar,
       uc_1_wmdr, uc_1_wmem, uc_1_wpc, uc_1_wreg;
  wire [2:0] ir_1_dout, ir_1_dout_3;
  wire [3:0] alu_1_flagout, sr_1_cout, uc_1_aluop0;
  wire [7:0] ac_1_dhout, alu_1_result, mar_1_dout, mdr_1_dout, memdata_1_dout, multiplexer_1_out, pc_1_dout,
       registerfile_1_raout, registerfile_1_rbout;
  wire [7:3] ir_1_dout_2;
  wire [15:0] memcode_1_d;
  wire [15:11] ir_1_dout_4;

  REGISTERFILE registerfile_1 (
    .CLK(CLOCK_out), .W(uc_1_wreg), .WSEL(ir_1_dout_3), .DIN(ac_1_dhout), .RAOUT(registerfile_1_raout),
    .RASEL(ir_1_dout_3), .RBOUT(registerfile_1_rbout), .RBSEL(ir_1_dout));
  SR sr_1 (
    .CLK(CLOCK_out), .W(uc_1_srw), .VIN(alu_1_flagout[3]), .NIN(alu_1_flagout[2]), .ZIN(alu_1_flagout[1]),
    .CIN(alu_1_flagout[0]), .VOUT(sr_1_cout[3]), .NOUT(sr_1_cout[2]), .ZOUT(sr_1_cout[1]), .COUT(sr_1_cout[0]));
  ALU alu_1 (
    .FLAGIN(sr_1_cout), .OP(uc_1_aluop0), .FLAGOUT(alu_1_flagout), .A(registerfile_1_raout),
    .B(multiplexer_1_out), .RESULT(alu_1_result));
  AC ac_1 (.R(uc_1_rac), .DIN(alu_1_result), .W(uc_1_wac), .CLK(CLOCK_out), .DHOUT(ac_1_dhout));
  LED STOP (.in(uc_1_stop));
  Multiplexer #(.width(8), .enable("false")) multiplexer_1 (
    .in0(registerfile_1_rbout), .in1({ir_1_dout_2, ir_1_dout}), .out(multiplexer_1_out), .sel(uc_1_inm));
  UC uc_1 (
    .CLK(CLOCK_out), .RESET(RESET___START_out), .WREG(uc_1_wreg), .ALUOP3(uc_1_aluop0[3]),
    .ALUOP2(uc_1_aluop0[2]), .ALUOP1(uc_1_aluop0[1]), .ALUOP0(uc_1_aluop0[0]), .RAC(uc_1_rac),
    .WAC(uc_1_wac), .SRW(uc_1_srw), .INM(uc_1_inm), .RSP(uc_1_rsp), .DSP(uc_1_dsp), .ISP(uc_1_isp),
    .IPC(uc_1_ipc), .RPC(uc_1_rpc), .WPC(uc_1_wpc), .WIR(uc_1_wir), .RMEM(uc_1_rmem), .WMEM(uc_1_wmem),
    .I_OMDR(uc_1_i_omdr), .WMDR(uc_1_wmdr), .WMAR(uc_1_wmar),
    .IR({ir_1_dout_4, ir_1_dout_3, ir_1_dout_2, ir_1_dout}), .STOP(uc_1_stop), .FLAGS(sr_1_cout),
    .CSP(uc_1_csp), .CPC(uc_1_cpc));
  SP sp_1 (.D(uc_1_dsp), .I(uc_1_isp), .CLK(CLOCK_out), .DHOUT(ac_1_dhout), .R(uc_1_rsp), .C(uc_1_csp));
  IR ir_1 (.DIN(memcode_1_d), .DOUT({ir_1_dout_4, ir_1_dout_3, ir_1_dout_2, ir_1_dout}), .W(uc_1_wir), .CLK(CLOCK_out));
  MEMCODE memcode_1 (.A(pc_1_dout), .D(memcode_1_d));
  PC pc_1 (
    .W(uc_1_wpc), .DIN(ac_1_dhout), .CLK(CLOCK_out), .I(uc_1_ipc), .DOUT(pc_1_dout), .C(uc_1_cpc),
    .DHOUT(ac_1_dhout), .R(uc_1_rpc));
  Button RESET___START (.out(RESET___START_out));
  MDR mdr_1 (
    .DHIN(ac_1_dhout), .DOUT(mdr_1_dout), .DHOUT(ac_1_dhout), .DIN(memdata_1_dout), .W(uc_1_wmdr),
    .I_O(uc_1_i_omdr), .CLK(CLOCK_out));
  Clock CLOCK (.out(CLOCK_out));
  MEMDATA memdata_1 (
    .A(mar_1_dout), .W(uc_1_wmem), .R(uc_1_rmem), .DOUT(memdata_1_dout), .CLK(CLOCK_out), .DIN(mdr_1_dout));
  MAR mar_1 (.DHIN(ac_1_dhout), .W(uc_1_wmar), .CLK(CLOCK_out), .DOUT(mar_1_dout));
endmodule

module PC (
  input  W,
  input  C,
  input  [7:0] DIN,
  input  R,
  input  I,
  input  CLK,
  output [7:0] DOUT,
  output [7:0] DHOUT
);

  wire or_1_out;
  wire [7:0] multiplexer_1_out;

  or or_1 (or_1_out, W, C);
  Counter counter_1 (.load(or_1_out), .D(multiplexer_1_out), .count(I), .Q(DOUT), .clk(CLK));  // open: carry, clr
  Multiplexer #(.width(8), .disabled(0), .enable("false")) multiplexer_1 (
    .in0(DIN), .in1({8{1'b0}}), .out(multiplexer_1_out), .sel(C));
  Transistor #(.\type ("n"), .width(8)) transistor_1 (.in(DOUT), .out(DHOUT), .gate(R));
endmodule

module MEMCODE (
  input  [7:0] A,
  output [15:0] D
);

  ROM #(.dataWidth(16)) rom_1 (.addr(A), .data(D), .sel(1'b1));
endmodule

module IR (
  input  [15:0] DIN,
  input  W,
  input  CLK,
  output [15:0] DOUT
);

  Register #(.width(16)) register_1 (.D(DIN), .en(W), .Q(DOUT), .clk(CLK));  // open: clr
endmodule

module MDR (
  input  [7:0] DHIN,
  input  [7:0] DIN,
  input  CLK,
  input  W,
  input  I_O,
  output [7:0] DOUT,
  output [7:0] DHOUT
);

  wire and_1_out;
  wire [7:0] multiplexer_1_out;

  Multiplexer #(.width(8), .disabled(0), .enable("false")) multiplexer_1 (
    .in0(DHIN), .in1(DIN), .out(multiplexer_1_out), .sel(I_O));
  Register register_1 (.D(multiplexer_1_out), .en(W), .Q(DOUT), .clk(CLK));  // open: clr
  Transistor #(.\type ("n"), .gate("br"), .width(8)) transistor_1 (.in(DOUT), .out(DHOUT), .gate(and_1_out));
  and and_1 (and_1_out, ~W, I_O);  // AND_Gate
endmodule

module MAR (
  input  [7:0] DHIN,
  input  W,
  input  CLK,
  output [7:0] DOUT
);

  Register register_1 (.D(DHIN), .en(W), .Q(DOUT), .clk(CLK));  // open: clr
endmodule

module MEMDATA (
  input  [7:0] A,
  input  [7:0] DIN,
  input  W,
  input  CLK,
  input  R,
  output [7:0] DOUT
);

  RAM #(.bus("separate")) ram_1 (.addr(A), .din(DIN), .data(DOUT), .str(W), .clk(CLK), .ld(R));  // open: sel, clr
endmodule

module SP (
  input  C,
  input  R,
  input  D,
  input  I,
  input  CLK,
  output [7:0] DHOUT
);

  wire or_1_out, or_2_out;
  wire [7:0] counter_1_q;

  or or_1 (or_1_out, C, D);
  or or_2 (or_2_out, D, I);
  Transistor #(.\type ("n"), .width(8)) transistor_1 (.in(counter_1_q), .out(DHOUT), .gate(R));
  Counter counter_1 (.load(or_1_out), .D({8{1'b1}}), .count(or_2_out), .Q(counter_1_q), .clk(CLK));  // open: carry, clr
endmodule

module AC (
  input  [7:0] DIN,
  input  W,
  input  R,
  input  CLK,
  output [7:0] DHOUT
);

  wire [7:0] register_1_q;

  Transistor #(.\type ("n"), .gate("br"), .width(8)) transistor_1 (.in(register_1_q), .out(DHOUT), .gate(R));
  Register register_1 (.D(DIN), .en(W), .Q(register_1_q), .clk(CLK));  // open: clr
endmodule

module SR (
  input  W,
  input  CLK,
  input  VIN,
  input  NIN,
  input  ZIN,
  input  CIN,
  output VOUT,
  output NOUT,
  output ZOUT,
  output COUT
);

  D_Flip_Flop V (.clk(CLK), .D(VIN), .Q(VOUT), .en(W));  // open: Qn, preset, reset
  D_Flip_Flop N (.clk(CLK), .D(NIN), .Q(NOUT), .en(W));  // open: Qn, preset, reset
  D_Flip_Flop Z (.clk(CLK), .D(ZIN), .Q(ZOUT), .en(W));  // open: Qn, preset, reset
  D_Flip_Flop C (.clk(CLK), .D(CIN), .Q(COUT), .en(W));  // open: Qn, preset, reset
endmodule

module REGISTERFILE (
  input  CLK,
  input  [2:0] RASEL,
  input  W,
  input  [2:0] WSEL,
  input  [2:0] RBSEL,
  input  [7:0] DIN,
  output [7:0] RAOUT,
  output [7:0] RBOUT
);

  wire demultiplexer_1_out0, demultiplexer_1_out1, demultiplexer_1_out2, demultiplexer_1_out3,
       demultiplexer_1_out4, demultiplexer_1_out5, demultiplexer_1_out6, demultiplexer_1_out7;
  wire [7:0] R0_q, R1_q, R2_q, R3_q, R4_q, R5_q, R6_q, R7_q;

  Demultiplexer #(.select(3), .disabled(0), .enable("false")) demultiplexer_1 (
    .out0(demultiplexer_1_out0), .out1(demultiplexer_1_out1), .out2(demultiplexer_1_out2),
    .out3(demultiplexer_1_out3), .out4(demultiplexer_1_out4), .out5(demultiplexer_1_out5),
    .out6(demultiplexer_1_out6), .out7(demultiplexer_1_out7), .in(W), .sel(WSEL));
  Register R0 (.D(DIN), .en(demultiplexer_1_out0), .Q(R0_q), .clk(CLK));  // open: clr
  Register R1 (.D(DIN), .en(demultiplexer_1_out1), .Q(R1_q), .clk(CLK));  // open: clr
  Register R2 (.D(DIN), .en(demultiplexer_1_out2), .Q(R2_q), .clk(CLK));  // open: clr
  Register R3 (.D(DIN), .en(demultiplexer_1_out3), .Q(R3_q), .clk(CLK));  // open: clr
  Register R4 (.D(DIN), .en(demultiplexer_1_out4), .Q(R4_q), .clk(CLK));  // open: clr
  Register R5 (.D(DIN), .en(demultiplexer_1_out5), .Q(R5_q), .clk(CLK));  // open: clr
  Register R6 (.D(DIN), .en(demultiplexer_1_out6), .Q(R6_q), .clk(CLK));  // open: clr
  Register R7 (.D(DIN), .en(demultiplexer_1_out7), .Q(R7_q), .clk(CLK));  // open: clr
  Multiplexer #(.select(3), .width(8), .enable("false")) multiplexer_1 (
    .in0(R0_q), .in1(R1_q), .in2(R2_q), .in3(R3_q), .in4(R4_q), .in5(R5_q), .in6(R6_q), .in7(R7_q),
    .out(RAOUT), .sel(RASEL));
  Multiplexer #(.select(3), .width(8), .enable("false")) multiplexer_2 (
    .in0(R0_q), .in1(R1_q), .in2(R2_q), .in3(R3_q), .in4(R4_q), .in5(R5_q), .in6(R6_q), .in7(R7_q),
    .out(RBOUT), .sel(RBSEL));
endmodule

module ALU (
  input  [3:0] FLAGIN,
  input  [3:0] OP,
  input  [7:0] A,
  input  [7:0] B,
  output [7:0] RESULT,
  output [3:0] FLAGOUT
);

  wire [3:0] alu_8adder_1_c;
  wire [3:1] xor_2_out;
  wire [3:3] xor_1_out;
  wire [7:0] alu_8adder_1_result, alu_lshifter_1_out, alu_rshifter_1_out;

  xor xor_1 (xor_1_out[3], A[6], A[7]);
  xor xor_2 (xor_2_out[3], FLAGIN[0], A[7]);
  Multiplexer #(.select(4), .width(4), .disabled(0), .enable("false")) multiplexer_1 (
    .in0({FLAGIN[3:1], OP[0]}), .in1({FLAGIN[3:1], OP[0]}), .in2({FLAGIN[3:1], OP[0]}),
    .in3({FLAGIN[3:1], OP[0]}), .in4({xor_2_out[3], RESULT[7], xor_2_out[1], A[0]}),
    .in5({xor_1_out[3], RESULT[7], xor_2_out[1], A[7]}),
    .in6({alu_8adder_1_c[3], RESULT[7], xor_2_out[1], alu_8adder_1_c[0]}),
    .in7({alu_8adder_1_c[3], RESULT[7], xor_2_out[1], alu_8adder_1_c[0]}),
    .in8({alu_8adder_1_c[3], RESULT[7], xor_2_out[1], alu_8adder_1_c[0]}),
    .in9({alu_8adder_1_c[3], RESULT[7], xor_2_out[1], alu_8adder_1_c[0]}),
    .in10({alu_8adder_1_c[3], RESULT[7], xor_2_out[1], alu_8adder_1_c[0]}),
    .in11({alu_8adder_1_c[3], RESULT[7], xor_2_out[1], alu_8adder_1_c[0]}),
    .in12({alu_8adder_1_c[3], RESULT[7], xor_2_out[1], alu_8adder_1_c[0]}),
    .in13({alu_8adder_1_c[3], RESULT[7], xor_2_out[1], alu_8adder_1_c[0]}),
    .in14({alu_8adder_1_c[3], RESULT[7], xor_2_out[1], alu_8adder_1_c[0]}),
    .in15({alu_8adder_1_c[3], RESULT[7], xor_2_out[1], alu_8adder_1_c[0]}), .out(FLAGOUT), .sel(OP));
  and and_1 (xor_2_out[1], ~RESULT[0], ~RESULT[1], ~RESULT[2], ~RESULT[3], ~RESULT[4], ~RESULT[5], ~RESULT[6], ~RESULT[7]);  // AND_Gate
  ALU_RSHIFTER alu_rshifter_1 (.IN(A), .OUT(alu_rshifter_1_out), .CIN(FLAGIN[0]));
  ALU_LSHIFTER alu_lshifter_1 (.IN(A), .OUT(alu_lshifter_1_out), .CIN(FLAGIN[0]));
  Multiplexer #(.select(4), .width(8), .disabled(0), .enable("false")) multiplexer_2 (
    .in0({8{1'b0}}), .in1({8{1'b0}}), .in2({8{1'b0}}), .in3({8{1'b0}}), .in4(alu_rshifter_1_out),
    .in5(alu_lshifter_1_out), .in6(A), .in7(A), .in8(alu_8adder_1_result), .in9(alu_8adder_1_result),
    .in10(alu_8adder_1_result), .in11(alu_8adder_1_result), .in12(B), .in13(B), .in14(B), .in15(B),
    .out(RESULT), .sel(OP));
  ALU_8ADDER alu_8adder_1 (
    .B(B), .A(A), .C(alu_8adder_1_c[0]), .V(alu_8adder_1_c[3]), .RESULT(alu_8adder_1_result), .S_R(OP[1]));
endmodule

// 8ADDER
module ALU_8ADDER (
  input  S_R,
  input  [7:0] B,
  input  [7:0] A,
  output C,
  output V,
  output [7:0] RESULT
);

  wire adder_1_cout, adder_2_cout, adder_3_cout, adder_4_cout, adder_5_cout, adder_6_cout, adder_7_cout;
  wire [7:0] multiplexer_1_out, not_1_out;

  assign not_1_out = ~B;  // NOT_Gate not_1, 8 bits wide
  Multiplexer #(.width(8), .enable("false")) multiplexer_1 (
    .in0(B), .in1(not_1_out), .out(multiplexer_1_out), .sel(S_R));
  Adder #(.width(1)) adder_1 (.a(multiplexer_1_out[0]), .b(A[0]), .out(RESULT[0]), .cin(S_R), .cout(adder_1_cout));
  Adder #(.width(1)) adder_2 (
    .a(multiplexer_1_out[1]), .b(A[1]), .out(RESULT[1]), .cin(adder_1_cout), .cout(adder_2_cout));
  Adder #(.width(1)) adder_3 (
    .a(multiplexer_1_out[2]), .b(A[2]), .out(RESULT[2]), .cin(adder_2_cout), .cout(adder_3_cout));
  Adder #(.width(1)) adder_4 (
    .a(multiplexer_1_out[3]), .b(A[3]), .out(RESULT[3]), .cin(adder_3_cout), .cout(adder_4_cout));
  Adder #(.width(1)) adder_5 (
    .a(multiplexer_1_out[4]), .b(A[4]), .out(RESULT[4]), .cin(adder_4_cout), .cout(adder_5_cout));
  Adder #(.width(1)) adder_6 (
    .a(multiplexer_1_out[5]), .b(A[5]), .out(RESULT[5]), .cin(adder_5_cout), .cout(adder_6_cout));
  Adder #(.width(1)) adder_7 (
    .a(multiplexer_1_out[6]), .b(A[6]), .out(RESULT[6]), .cin(adder_6_cout), .cout(adder_7_cout));
  Adder #(.width(1)) adder_8 (.a(multiplexer_1_out[7]), .b(A[7]), .out(RESULT[7]), .cin(adder_7_cout), .cout(C));
  xor xor_1 (V, C, adder_7_cout);
endmodule

// RSHIFT
module ALU_RSHIFTER (
  input  [7:0] IN,
  input  CIN,
  output [7:0] OUT
);


  assign OUT = {CIN, IN[7:1]};
endmodule

// LSHIFT
module ALU_LSHIFTER (
  input  CIN,
  input  [7:0] IN,
  output [7:0] OUT
);


  assign OUT = {IN[6:0], CIN};
endmodule

module UC (
  input  [3:0] FLAGS,
  input  [15:0] IR,
  input  CLK,
  input  RESET,
  output STOP,
  output WREG,
  output ALUOP3,
  output ALUOP2,
  output ALUOP1,
  output ALUOP0,
  output RAC,
  output WAC,
  output SRW,
  output INM,
  output RSP,
  output CSP,
  output DSP,
  output ISP,
  output IPC,
  output CPC,
  output RPC,
  output WPC,
  output WIR,
  output RMEM,
  output WMEM,
  output I_OMDR,
  output WMDR,
  output WMAR
);

  wire not_1_out;
  wire [1:0] uc_bootup_1_boot;
  wire [5:0] adder_1_out, counter_1_q, multiplexer_1_out, multiplexer_2_out;
  wire [23:23] rom_1_data;

  Multiplexer #(.select(5), .width(6), .enable("false")) multiplexer_1 (
    .in0({6{1'b0}}), .in1(6'b000100), .in2(6'b001000), .in3(6'b001100), .in4(6'b010000), .in5(6'b010100),
    .in6(6'b011001), .in7(6'b011100), .in8(6'b011111), .in9(6'b110101), .in10(6'b100001), .in11(6'b100011),
    .in12(6'b110101), .in13(6'b110101), .in14(6'b110101), .in15(6'b100100), .in16(6'b110101),
    .in17(6'b110101), .in18(6'b100110), .in19(6'b100111), .in20(6'b101000), .in21(6'b101010),
    .in22(6'b110101), .in23(6'b101100), .in24(6'b101101), .in25(6'b110101), .in26(6'b101111),
    .in27(6'b110001), .in28(6'b110101), .in29(6'b110101), .in30(6'b110101), .in31(6'b110010),
    .out(multiplexer_1_out), .sel(IR[15:11]));
  UC_LOGIC uc_logic_1 (.FLAGS(FLAGS), .KEEP(uc_bootup_1_boot[1]), .IR(IR), .STOP(STOP));
  UC_BOOTUP uc_bootup_1 (.CLK(CLK), .RESET(RESET), .BOOT(uc_bootup_1_boot[0]));
  Multiplexer #(.select(2), .width(6), .disabled(0), .enable("false")) multiplexer_2 (
    .in1(6'b110101), .in2(6'b110100), .in3(multiplexer_1_out), .out(multiplexer_2_out), .sel(uc_bootup_1_boot));  // open: in0
  not not_1 (not_1_out, rom_1_data[23]);
  Adder #(.width(6)) adder_1 (.a(multiplexer_2_out), .b(counter_1_q), .out(adder_1_out));  // open: cin, cout
  Counter #(.width(6), .max('h3f)) counter_1 (
    .load(rom_1_data[23]), .D({6{1'b0}}), .count(not_1_out), .Q(counter_1_q), .clk(CLK), .clr(RESET));  // open: carry
  ROM #(.addrWidth(6), .dataWidth(24)) rom_1 (
    .addr(adder_1_out),
    .data({rom_1_data[23], WREG, ALUOP3, ALUOP2, ALUOP1, ALUOP0, RAC, WAC, SRW, INM, RSP, CSP, DSP, ISP, IPC, CPC, RPC, WPC, WIR, RMEM, WMEM, I_OMDR, WMDR, WMAR}));  // open: sel

  // Notes on the sheet:
  //   KEEP
  //   END
  //   contents of rom_1 (hex, n*v repeats v):
  //   310000 1b0001 20002 800228 310000 1b0001 16 c00224 314000 1b0001 20002 800228 314000 1b0001 16
  //   c00224 314082 2801 20048 800220 314400 2001 16 44 800220 314000 20040 800220 314000 20040 800220
  //   218000 c20220 298000 c20220 a98220 310000 c20220 808220 8c8220 11c000 c20220 15c000 c20220 800000
  //   21c000 c20220 29c000 c20220 a9c220 314000 c20220 1100 800220
endmodule

// LOGIC
module UC_LOGIC (
  input  [15:0] IR,
  input  [3:0] FLAGS,
  output KEEP,
  output STOP
);

  wire and_2_out, multiplexer_1_out, not_1_out, not_2_out, not_3_out, not_4_out, not_5_out, not_6_out,
       xor_1_out;

  not not_1 (not_1_out, IR[14]);
  and and_1 (STOP, IR[15], not_1_out, IR[13], IR[12], IR[11]);
  not not_2 (not_2_out, IR[11]);
  not not_3 (not_3_out, IR[14]);
  not not_4 (not_4_out, IR[15]);
  and and_2 (and_2_out, not_4_out, not_3_out, IR[13], IR[12], not_2_out);
  or or_1 (KEEP, not_5_out, multiplexer_1_out);
  not not_5 (not_5_out, and_2_out);
  Multiplexer #(.select(2), .disabled(0), .enable("false")) multiplexer_1 (
    .in0(FLAGS[1]), .in1(not_6_out), .in2(FLAGS[3]), .in3(xor_1_out), .out(multiplexer_1_out), .sel(IR[9:8]));
  not not_6 (not_6_out, FLAGS[0]);
  xor xor_1 (xor_1_out, FLAGS[3], FLAGS[2]);

  // Notes on the sheet:
  //   VNZC
endmodule

// BOOT
module UC_BOOTUP (
  input  CLK,
  input  RESET,
  output BOOT
);

  wire [0:0] counter_1_q;

  Counter #(.width(2), .max('h2), .ongoal("stay")) counter_1 (
    .count(CLK), .Q({BOOT, counter_1_q[0]}), .clk(CLK), .clr(RESET));  // open: load, D, carry
endmodule
